// Logisim project practice.circ as structural Verilog
module Q1 (
  input  CB,
  input  DB,
  input  DA,
  input  BA,
  input  BB,
  input  BC,
  input  A,
  input  B,
  input  C,
  input  D,
  input  DC,
  input  CA,
  output Z
);

  wire nand_1_out, nand_2_out, not_1_out, not_2_out, or_1_out, or_2_out, or_3_out, or_4_out;

  or or_1 (or_1_out, C, D);
  not not_1 (not_1_out, B);
  or or_2 (or_2_out, not_1_out, C);
  or or_3 (or_3_out, B, D);
  or or_4 (or_4_out, A, B, not_2_out);
  not not_2 (not_2_out, C);
  nand nand_1 (nand_1_out, or_1_out, or_2_out);
  nand nand_2 (nand_2_out, or_3_out, or_4_out);
  or or_5 (Z, nand_1_out, nand_2_out);
endmodule

module Q1SOP (
  input  CB,
  input  DB,
  input  DA,
  input  BA,
  input  BB,
  input  BC,
  input  A,
  input  B,
  input  C,
  input  D,
  input  DC,
  input  CA,
  output Z
);

  wire and_1_out, and_2_out, and_3_out, not_1_out, not_2_out, not_3_out, not_4_out, not_5_out;

  not not_1 (not_1_out, B);
  and and_1 (and_1_out, not_1_out, not_2_out);
  not not_2 (not_2_out, D);
  not not_3 (not_3_out, C);
  and and_2 (and_2_out, not_3_out, B);
  not not_4 (not_4_out, A);
  and and_3 (and_3_out, not_4_out, not_5_out, C);
  not not_5 (not_5_out, B);
  or or_1 (Z, and_1_out, and_2_out, and_3_out);
endmodule

module Q1SOP2 (
  input  A,
  input  B,
  input  C,
  input  D,
  output Z
);

  wire and_1_out, and_2_out, and_3_out, and_4_out, not_1_out, not_2_out, not_3_out, not_4_out, not_5_out,
       not_6_out;

  not not_1 (not_1_out, C);
  and and_1 (and_1_out, not_1_out, D);
  and and_2 (and_2_out, B, not_2_out);
  not not_2 (not_2_out, C);
  not not_3 (not_3_out, B);
  and and_3 (and_3_out, not_3_out, not_4_out);
  not not_4 (not_4_out, D);
  not not_5 (not_5_out, A);
  and and_4 (and_4_out, not_5_out, not_6_out, C);
  not not_6 (not_6_out, B);
  or or_1 (Z, and_1_out, and_2_out, and_3_out, and_4_out);
endmodule
